// Logisim project prevodnik-cisel_+3.circ as structural Verilog: 1 circuit, main circuit main
module main (
  input  in_1,
  input  in_2,
  input  in_3,
  input  in_4
);

  wire nand_1_out, nand_2_out, nand_3_out, nand_4_out, nand_5_out, nand_6_out, nand_7_out, nand_8_out,
       nand_9_out, nand_10_out, not_1_out, not_2_out, not_3_out, not_4_out;

  not not_1 (not_1_out, in_1);
  not not_2 (not_2_out, in_2);
  not not_3 (not_3_out, in_3);
  not not_4 (not_4_out, in_4);
  nand nand_1 (nand_1_out, in_3, in_1);
  nand nand_2 (nand_2_out, in_2, in_3);
  nand nand_3 (nand_3_out, in_1, not_3_out);
  nand nand_4 (nand_4_out, in_2, not_3_out);
  nand nand_5 (nand_5_out, not_1_out, not_2_out, in_3);
  nand nand_6 (nand_6_out, not_1_out, not_2_out);
  nand nand_7 (nand_7_out, in_1, in_2);
  nand nand_8 (nand_8_out, not_4_out, nand_1_out, nand_2_out);
  nand nand_9 (nand_9_out, nand_3_out, nand_4_out, nand_5_out);
  nand nand_10 (nand_10_out, nand_6_out, nand_7_out);
  LED led_1 (.in(nand_8_out));
  LED led_2 (.in(nand_9_out));
  LED led_3 (.in(nand_10_out));
  LED led_4 (.in(not_1_out));
endmodule
