// Logisim project 7segm5-NAND-only.circ as structural Verilog: 1 circuit, main circuit main
module main (
  input  b0,
  input  b1,
  input  b2,
  input  b3
);

  wire _7420a_out, b_out, d_out, e_out, f_out, g_out, nand_1_out, nand_2_out, nand_3_out, nand_4_out,
       nand_5_out, nand_6_out, nand_7_out, nand_8_out, nand_9_out, not_1_out, not_2_out, not_3_out, not_4_out;

  not not_1 (not_1_out, b0);
  not not_2 (not_2_out, b1);
  not not_3 (not_3_out, b2);
  not not_4 (not_4_out, b3);
  nand nand_1 (nand_1_out, b0, not_2_out, not_3_out, not_4_out);
  nand nand_2 (nand_2_out, not_1_out, b1, b2);
  nand nand_3 (nand_3_out, not_2_out, b0, b2);
  nand nand_4 (nand_4_out, not_1_out, b1, not_3_out);
  nand nand_5 (nand_5_out, b2, not_1_out, not_2_out);
  nand nand_6 (nand_6_out, b2, b1, b0);
  nand nand_7 (nand_7_out, b0, not_3_out, not_4_out);
  nand nand_8 (nand_8_out, not_2_out, not_3_out, not_4_out);
  nand nand_9 (nand_9_out, nand_1_out, nand_5_out);
  nand b (b_out, nand_2_out, nand_3_out);
  nand _7420a (_7420a_out, nand_4_out, nand_4_out, nand_4_out, nand_4_out);
  nand d (d_out, nand_1_out, nand_5_out, nand_6_out);
  nand e (e_out, nand_5_out, not_1_out);
  nand f (f_out, nand_4_out, nand_6_out, nand_7_out);
  nand g (g_out, nand_6_out, nand_8_out);
  _7_Segment_Display #(.active("false")) u_7_segment_display_1 (
    .g(g_out), .f(f_out), .a(nand_9_out), .b(b_out), .e(e_out), .d(d_out), .c(_7420a_out));  // open: dp

  // Notes on the sheet:
  //   1
  //   7420a
  //   2
  //   4
  //   5
  //   1
  //   7410a1
  //   2
  //   13
  //   3
  //   7410b1
  //   4
  //   5
  //   11
  //   7410c1
  //   10
  //   9
  //   1
  //   7410a2
  //   2
  //   13
  //   3
  //   7410b2
  //   4
  //   5
  //   11
  //   7410c2
  //   10
  //   9
  //   1
  //   7410a3
  //   2
  //   13
  //   Prevodník BCD na 7seg. displej
  //   6
  //   12
  //   6
  //   8
  //   12
  //   6
  //   8
  //   12
  //   1
  //   7400a1
  //   a
  //   2
  //   4
  //   7400b1
  //   5
  //   9
  //   10
  //   12
  //   13
  //   3
  //   7410b3
  //   4
  //   5
  //   10
  //   7400c1
  //   9
  //   11
  //   7410c3
  //   10
  //   9
  //   12
  //   7400d1
  //   13
  //   3
  //   6
  //   8
  //   6
  //   8
  //   8
  //   11
  //   by:
  //   Potreba:
  //   1x NAND 7420
  //   3x NAND 7410
  //   1x NAND 7400
  //   g
  //   a
  //   f
  //   e
  //   d
  //   c
  //   Dobroslav Grygar
  //   Filip Kubala
  //   Jakub Hričovský
  //   Andrej Šišila
  //   b
  //   bodka
endmodule
