// Logisim project ParkoviskoPre2Auta.circ as structural Verilog: 1 circuit, main circuit main
module main (
  input  A,
  input  B
);

  wire _1_2_out, _1_out, _2_2_out, _2_out, button_1_out, button_2_out, d_ff_1_q, d_ff_1_qn, d_ff_2_q,
       d_ff_2_qn, nand_1_out, nand_2_out, nand_3_out, nand_4_out, not_1_out, not_2_out, undriven;

  Button button_1 (.out(button_1_out));
  Button button_2 (.out(button_2_out));
  not not_1 (not_1_out, A);
  not not_2 (not_2_out, B);
  nand nand_1 (nand_1_out, d_ff_1_q, d_ff_2_qn);
  nand nand_2 (nand_2_out, d_ff_1_q, B);
  nand _1 (_1_out, d_ff_2_q, A, not_2_out);
  nand nand_3 (nand_3_out, d_ff_1_q, A);
  nand nand_4 (nand_4_out, d_ff_2_q, not_2_out);
  nand _1_2 (_1_2_out, d_ff_1_qn, not_1_out, B);
  nand _2 (_2_out, nand_1_out, nand_2_out, _1_out);
  nand _2_2 (_2_2_out, nand_3_out, nand_4_out, _1_2_out);
  D_Flip_Flop #(.trigger("high")) d_ff_1 (
    .clk(button_1_out), .D(_2_out), .Q(d_ff_1_q), .Qn(d_ff_1_qn), .preset(undriven), .reset(button_2_out));  // open: en
  D_Flip_Flop #(.trigger("high")) d_ff_2 (
    .clk(button_1_out), .D(_2_2_out), .Q(d_ff_2_q), .Qn(d_ff_2_qn), .preset(undriven), .reset(button_2_out));  // open: en
  LED led_1 (.in(d_ff_1_q));
  LED led_2 (.in(d_ff_1_qn));

  // Notes on the sheet:
  //   prepinac
  //   prepinac
  //   hodiny
  //   reset
  //   prepinac
  //   Parkovisko pre 2 autá
  //   prepinac
  //   z1
  //   z1n
  //   z2
  //   Vyjdenie auta, postupnosť vstupov: B1, clk, A1, clk, B0, clk, A0, clk...... Ak to spravis 2x tak je parkovisko je prazdne
  //   z2n
  //   1
  //   2
  //   4
  //   5
  //   1
  //   2
  //   13
  //   10
  //   9
  //   13
  //   12
  //   3
  //   4
  //   5
  //   Vojdenie auta, postupnosť vstupov: A1, clk, B1, clk, A0, clk, B0, clk ....... Ak to spravis 2x tak je parkovisko plne obsadene a ledna svieti na červeno
  //   7400
  //   3
  //   7400
  //   6
  //   7410
  //   12
  //   7400
  //   8
  //   7400
  //   11
  //   6
  //   7410
  //   1
  //   7410
  //   2
  //   13
  //   3
  //   7410
  //   4
  //   5
  //   set
  //   12
  //   6
  //   toto je spojené
  //   Vcc +5V real
  //   7474
  //   3
  //   5
  //   2
  //   6
  //   4
  //   1
  //   7474
  //   9
  //   11
  //   8
  //   12
  //   13
  //   10
  //   z1
  //   z1n
  //   z2
  //   z2n
  //   č
  //   z
  //   gnd
  //   ledka je len jedna
  //   pridať odpory (470)
  //   220 - 390 ohm
  //   Ak je zaplnene len jedno miesto, tak svieti zelena ledka
endmodule
