// Logisim project Vyrobky - uprava.circ as structural Verilog: 1 circuit, main circuit main
module main (
  input  A,
  input  B
);

  wire and_1_out, and_2_out, button_1_out, button_2_out, j_k_ff_1_q, j_k_ff_1_qn, nand_1_out, nand_2_out,
       nand_3_out, not_1_out, not_2_out, undriven;

  not not_1 (not_1_out, A);
  not not_2 (not_2_out, B);
  and and_1 (and_1_out, A, not_2_out, not_2_out);
  and and_2 (and_2_out, not_1_out, B, B);
  Button button_1 (.out(button_1_out));
  Button button_2 (.out(button_2_out));
  nand nand_1 (nand_1_out, j_k_ff_1_q, not_1_out, not_2_out);
  LED #(.active("false")) led_1 (.in(nand_1_out));
  nand nand_2 (nand_2_out, j_k_ff_1_q, A, B);
  LED #(.active("false")) led_2 (.in(nand_2_out));
  LED #(.active("false")) led_3 (.in(nand_3_out));
  nand nand_3 (nand_3_out, j_k_ff_1_qn, A, B);
  J_K_Flip_Flop j_k_ff_1 (
    .J(and_1_out), .clk(button_1_out), .K(and_2_out), .Q(j_k_ff_1_q), .Qn(j_k_ff_1_qn), .preset(undriven),
    .reset(button_2_out));  // open: en
  LED led_4 (.in(j_k_ff_1_q));

  // Notes on the sheet:
  //   b-clk-a-clk :svieti v3
  //   a-clk-a-clk :v1zasvieti
  //   a-clk-b-clk :v2 zasvieti
  //   b-clk-a-clk :v3 zasvieti
  //   z
  //   zn
  //   3
  //   4
  //   5
  //   9
  //   10
  //   11
  //   1
  //   2
  //   13
  //   7410
  //   3
  //   4
  //   5
  //   7410
  //   11
  //   10
  //   9
  //   7410
  //   b-clk-b-clk :v1 zhasne tj vyrobok presiel
  //   a-clk-b-clk :v2 zhasne
  //   a-clk-a-clk :v3 zasvieti
  //   12
  //   hodiny
  //   reset
  //   12
  //   6
  //   8
  //   13
  //   na pin 13 zapojit napatie
  //   v1
  //   v2
  //   v3
  //   8
  //   6
  //   2
  //   7472
  //   v1-v3 do segmentovky do vodorovnych segmentov
  //   vrchna ledka siignalizuje stavy automatu
  //   v1-v3 su typy vyrobkov
endmodule
