// Logisim project 7segm5-NAND-only-edit.circ as structural Verilog: 1 circuit, main circuit main
module main (
  input  b0,
  input  b1,
  input  b2,
  input  b3
);

  wire _7400_2_out, _7400_3_out, _7400_4_out, _7400_out, _7410_A_2_out, _7410_A_3_out, _7410_A_out,
       _7410_B_2_out, _7410_B_3_out, _7410_B_out, _7410_C_2_out, _7410_C_3_out, _7410_C_out, _7420_2_out,
       _7420_out, not_1_out, not_2_out, not_3_out, not_4_out;

  not not_1 (not_1_out, b0);
  not not_2 (not_2_out, b1);
  not not_3 (not_3_out, b2);
  not not_4 (not_4_out, b3);
  nand _7420 (_7420_out, b0, not_2_out, not_3_out, not_4_out);
  nand _7410_A (_7410_A_out, not_1_out, b1, b2);
  nand _7410_A_2 (_7410_A_2_out, not_2_out, b0, b2);
  nand _7410_A_3 (_7410_A_3_out, not_1_out, b1, not_3_out);
  nand _7410_B (_7410_B_out, b2, not_1_out, not_2_out);
  nand _7410_B_2 (_7410_B_2_out, b2, b1, b0);
  nand _7410_B_3 (_7410_B_3_out, b0, not_3_out, not_4_out);
  nand _7410_C (_7410_C_out, not_2_out, not_3_out, not_4_out);
  nand _7400 (_7400_out, _7420_out, _7410_B_out);
  nand _7400_2 (_7400_2_out, _7410_A_out, _7410_A_2_out);
  nand _7420_2 (_7420_2_out, _7410_A_3_out, _7410_A_3_out, _7410_A_3_out, _7410_A_3_out);
  nand _7410_C_2 (_7410_C_2_out, _7420_out, _7410_B_out, _7410_B_2_out);
  nand _7400_3 (_7400_3_out, _7410_B_out, not_1_out);
  nand _7410_C_3 (_7410_C_3_out, _7410_A_3_out, _7410_B_2_out, _7410_B_3_out);
  nand _7400_4 (_7400_4_out, _7410_B_2_out, _7410_C_out);
  _7_Segment_Display #(.active("false")) u_7_segment_display_1 (
    .g(_7400_4_out), .f(_7410_C_3_out), .a(_7400_out), .b(_7400_2_out), .e(_7400_3_out), .d(_7410_C_2_out),
    .c(_7420_2_out));  // open: dp

  // Notes on the sheet:
  //   1
  //   2
  //   4
  //   5
  //   1
  //   2
  //   13
  //   3
  //   4
  //   5
  //   11
  //   10
  //   9
  //   1
  //   2
  //   13
  //   3
  //   4
  //   5
  //   11
  //   10
  //   9
  //   1
  //   2
  //   13
  //   Prevodník BCD na 7seg. displej
  //   6
  //   12
  //   6
  //   8
  //   12
  //   6
  //   8
  //   12
  //   1
  //   2
  //   4
  //   5
  //   9
  //   10
  //   12
  //   13
  //   3
  //   4
  //   5
  //   10
  //   9
  //   11
  //   10
  //   9
  //   12
  //   13
  //   a
  //   3
  //   b
  //   6
  //   c
  //   8
  //   d
  //   6
  //   e
  //   8
  //   f
  //   8
  //   g
  //   11
  //   by:
  //   Potreba:
  //   1x NAND 7420
  //   3x NAND 7410
  //   1x NAND 7400
  //   a
  //   g
  //   f
  //   d
  //   e
  //   c
  //   Dobroslav Grygar
  //   Filip Kubala
  //   Jakub Hričovský
  //   Andrej Šišila
  //   b
  //   bodka
endmodule
